# Fritzing sketch button_report (saved by Fritzing 0.9.2b)
breadboards: 1

parts:
  T-Cobbler = T Cobbler Plus
  RaspberryPi2 = Raspberry Pi 2
  PushButtonSwitch01 = Momentary Switch [package=ksa_sealed_tac_switch]

nets:
  N1: T-Cobbler.GND#5, PushButtonSwitch01.1
  N2: T-Cobbler.#4, PushButtonSwitch01.4
  3V3: T-Cobbler.3.3V#41, T-Cobbler.3.3V#57, RaspberryPi2.3v3, RaspberryPi2.3V3
  5V: T-Cobbler.5V, RaspberryPi2.5V
  N3: T-Cobbler.GPIO_2, RaspberryPi2.GPIO2
  N4: T-Cobbler.GPIO_3, RaspberryPi2.GPIO3
  N5: T-Cobbler.GND#46, T-Cobbler.GND#49, T-Cobbler.GND#54, T-Cobbler.GND#60, T-Cobbler.GND#65, T-Cobbler.GND#70, T-Cobbler.GND#74, T-Cobbler.GND#79, RaspberryPi2.GND
  N6: T-Cobbler.GPIO_4, RaspberryPi2.GPIO4
  N7: T-Cobbler.GPIO_14, RaspberryPi2.GPIO14
  N8: T-Cobbler.GPIO_15, RaspberryPi2.GPIO15
  N9: T-Cobbler.GPIO_17, RaspberryPi2.GPIO17
  N10: T-Cobbler.GPIO_18, RaspberryPi2.GPIO18
  N11: T-Cobbler.GPIO_27, RaspberryPi2.GPIO27
  N12: T-Cobbler.GPIO_22, RaspberryPi2.GPIO22
  N13: T-Cobbler.GPIO_23, RaspberryPi2.GPIO23
  N14: T-Cobbler.GPIO_24, RaspberryPi2.GPIO24
  N15: T-Cobbler.GPIO_10, RaspberryPi2.GPIO10
  N16: T-Cobbler.GPIO_9, RaspberryPi2.GPIO9
  N17: T-Cobbler.GPIO_25, RaspberryPi2.GPIO25
  N18: T-Cobbler.GPIO_11, RaspberryPi2.GPIO11
  N19: T-Cobbler.GPIO_8, RaspberryPi2.GPIO8
  N20: T-Cobbler.GPIO_7, RaspberryPi2.GPIO7
  N21: T-Cobbler.ID_SD, RaspberryPi2.ID_SD
  N22: T-Cobbler.ID_SC, RaspberryPi2.ID_SC
  N23: T-Cobbler.GPIO_5, RaspberryPi2.GPIO5
  N24: T-Cobbler.GPIO_6, RaspberryPi2.GPIO6
  N25: T-Cobbler.GPIO_12, RaspberryPi2.GPIO12
  N26: T-Cobbler.GPIO_13, RaspberryPi2.GPIO13
  N27: T-Cobbler.GPIO_19, RaspberryPi2.GPIO19
  N28: T-Cobbler.GPIO_16, RaspberryPi2.GPIO16
  N29: T-Cobbler.GPIO_26, RaspberryPi2.GPIO26
  N30: T-Cobbler.GPIO_20, RaspberryPi2.GPIO20
  N31: T-Cobbler.GPIO_21, RaspberryPi2.GPIO21

custom parts:
  T Cobbler Plus: The T-Cobbler Plus is an add on prototyping board from Adafruit specifically designed for the Raspberry Pi B+ that can break out all those tasty power, GPIO, I2C and SPI pins from the 40-pin header onto a solderless breadboard. This set will make "cobbling together" prototypes with the Pi super easy. The T-Cobbler Plus can plug into any solderless breadboard.
