# Fritzing sketch led_blink (saved by Fritzing 0.9.2b)
breadboards: 1

parts:
  RaspberryPi3 = Raspberry Pi 2
  T-Cobbler1 = T Cobbler Plus
  LED2 = smd LED [color="Red (633nm)" package="1206 [SMD]"]
  R1 = Resistor [tolerance=±5% resistance=220 package="2010 [SMD]"]
  R2 = Resistor [tolerance=±5% resistance=220 package="2010 [SMD]"]
  LED3 = smd LED [color="Red (633nm)" package="1206 [SMD]"]
  R3 = Resistor [tolerance=±5% resistance=220 package="2010 [SMD]"]
  LED4 = smd LED [color="Red (633nm)" package="1206 [SMD]"]

nets:
  3V3: RaspberryPi3.3v3, RaspberryPi3.3V3, T-Cobbler1.3.3V#41, T-Cobbler1.3.3V#57
  N1: RaspberryPi3.GPIO2, T-Cobbler1.GPIO_2
  N2: RaspberryPi3.GPIO3, T-Cobbler1.GPIO_3
  N3: RaspberryPi3.GPIO4, T-Cobbler1.GPIO_4
  N4: RaspberryPi3.GND, T-Cobbler1.GND#46, T-Cobbler1.GND#49, T-Cobbler1.GND#54, T-Cobbler1.GND#60, T-Cobbler1.GND#65, T-Cobbler1.GND#70, T-Cobbler1.GND#74, T-Cobbler1.GND#79
  N5: RaspberryPi3.GPIO17, T-Cobbler1.GPIO_17
  N6: RaspberryPi3.GPIO27, T-Cobbler1.GPIO_27
  N7: RaspberryPi3.GPIO22, T-Cobbler1.GPIO_22
  N8: RaspberryPi3.GPIO10, T-Cobbler1.GPIO_10
  N9: RaspberryPi3.GPIO9, T-Cobbler1.GPIO_9
  N10: RaspberryPi3.GPIO11, T-Cobbler1.GPIO_11
  N11: RaspberryPi3.ID_SD, T-Cobbler1.ID_SD
  N12: RaspberryPi3.GPIO5, T-Cobbler1.GPIO_5
  N13: RaspberryPi3.GPIO6, T-Cobbler1.GPIO_6
  N14: RaspberryPi3.GPIO13, T-Cobbler1.GPIO_13
  N15: RaspberryPi3.GPIO19, T-Cobbler1.GPIO_19
  N16: RaspberryPi3.GPIO26, T-Cobbler1.GPIO_26
  N17: RaspberryPi3.GPIO21, T-Cobbler1.GPIO_21
  N18: RaspberryPi3.GPIO20, T-Cobbler1.GPIO_20
  N19: RaspberryPi3.GPIO16, T-Cobbler1.GPIO_16
  N20: RaspberryPi3.GPIO12, T-Cobbler1.GPIO_12
  N21: RaspberryPi3.ID_SC, T-Cobbler1.ID_SC
  N22: RaspberryPi3.GPIO7, T-Cobbler1.GPIO_7
  N23: RaspberryPi3.GPIO8, T-Cobbler1.GPIO_8
  N24: RaspberryPi3.GPIO25, T-Cobbler1.GPIO_25
  N25: RaspberryPi3.GPIO24, T-Cobbler1.GPIO_24
  N26: RaspberryPi3.GPIO23, T-Cobbler1.GPIO_23
  N27: RaspberryPi3.GPIO18, T-Cobbler1.GPIO_18
  N28: RaspberryPi3.GPIO15, T-Cobbler1.GPIO_15
  N29: RaspberryPi3.GPIO14, T-Cobbler1.GPIO_14
  5V: RaspberryPi3.5V, T-Cobbler1.5V
  N30: T-Cobbler1.GND#5, LED2.cathode, LED3.cathode, LED4.cathode
  N31: T-Cobbler1.#4, R1.Pin_0
  N32: T-Cobbler1.#17, R2.Pin_0
  N33: T-Cobbler1.#27, R3.Pin_0
  N34: LED2.anode, R1.Pin_1
  N35: R2.Pin_1, LED3.anode
  N36: R3.Pin_1, LED4.anode

custom parts:
  T Cobbler Plus: The T-Cobbler Plus is an add on prototyping board from Adafruit specifically designed for the Raspberry Pi B+ that can break out all those tasty power, GPIO, I2C and SPI pins from the 40-pin header onto a solderless breadboard. This set will make "cobbling together" prototypes with the Pi super easy. The T-Cobbler Plus can plug into any solderless breadboard.
